# Fritzing sketch rangefinder_with_serial (saved by Fritzing 0.9.3b)
breadboards: 1

parts:
  Raspberry_Pi_1 = Raspberry Pi 3 [part_number=RPI-3-V1.2]
  Part1 = Arduino Uno (Rev3)
  LCD1 = LCD screen
  J1 = Infrared Proximity Sensor
  R1 = Resistor [tolerance=±5% resistance=220 package=THT]
  LED1 = LED - 3mm [color="Red (633nm)" package="3 mm [THT]"]

nets:
  N1: Raspberry_Pi_1.GPIO2, Part1.A4/SDA
  N2: Raspberry_Pi_1.GPIO3, Part1.A5/SCL
  GND: Raspberry_Pi_1.GND, Part1.GND, LCD1.VSS, J1.GND, R1.Pin_1, LED1.cathode, LED1.anode
  N3: Raspberry_Pi_1.GPIO14, LCD1.R/W
  N4: Part1.D5_PWM, R1.Pin_0
  N5: Part1.D7, J1.Vout
  3V3: Part1.3V3, LCD1.VDD
  5V: Part1.5V, J1.Vcc

notes:
  This is a serial-enabled LCD display. Standard display with a serial backpack. The backpack has only 3 connections: 3.3 v, GND, and RX.
